# Fritzing sketch elbow-rehab (saved by Fritzing 0.9.5d)
breadboards: 1

parts:
  ESP_32-C6_DEVKIT_V1 = ESP32-C6 devkit
  STEP_DOWN_5V = DC_DC_XL4016 [package=board_screw]
  PSU_48V = Header 4 [package=screwterminal-3.5mm-4_lock]
  E-STOP = Square Pushbutton
  SENSOR_SUDUT_AS5600 = AS5600 module
  LCD_20X4 = LCD2004-I2C
  BACK = Round Pushbutton
  STOP = Round Pushbutton
  MODE = Round Pushbutton
  OK = Round Pushbutton
  ZERO = Round Pushbutton
  LIMIT_ATAS = JL012-13-5.2 Lever (Limit) Switch SPDT + NO + NC [part_number=JL012-13-5.2]
  LIMIT_BAWAH = JL012-13-5.2 Lever (Limit) Switch SPDT + NO + NC [part_number=JL012-13-5.2]
  Q1 = NPN-Transistor [package="TO92 [THT]"]
  Q2 = NPN-Transistor [package="TO92 [THT]"]
  Q3 = NPN-Transistor [package="TO92 [THT]"]
  R1 = Resistor [tolerance=±5% resistance=1k package=THT]
  R2 = Resistor [tolerance=±5% resistance=1k package=THT]
  R3 = Resistor [tolerance=±5% resistance=1k package=THT]
  R4 = Resistor [tolerance=±5% resistance=10k package=THT]
  R5 = Resistor [tolerance=±5% resistance=10k package=THT]
  R6 = Resistor [tolerance=±5% resistance=10k package=THT]
  DRIVER_HBS860H = Header 6 [package=1x06-smd_edge]

nets:
  VCC AS5600: ESP_32-C6_DEVKIT_V1.Pin_2
  SDA: ESP_32-C6_DEVKIT_V1.Pin_4
  SCL: ESP_32-C6_DEVKIT_V1.Pin_5
  N1: ESP_32-C6_DEVKIT_V1.Pin_8, ESP_32-C6_DEVKIT_V1.Pin_23
  BACK: ESP_32-C6_DEVKIT_V1.Pin_9, ESP_32-C6_DEVKIT_V1.Pin_22
  STOP: ESP_32-C6_DEVKIT_V1.Pin_11
  MODE/OK/OUT+/OUT-/Q1/ZERO: ESP_32-C6_DEVKIT_V1.Pin_12, ESP_32-C6_DEVKIT_V1.Pin_13, ESP_32-C6_DEVKIT_V1.Pin_14, ESP_32-C6_DEVKIT_V1.Pin_15, ESP_32-C6_DEVKIT_V1.Pin_16, ESP_32-C6_DEVKIT_V1.Pin_17, ESP_32-C6_DEVKIT_V1.Pin_18, ESP_32-C6_DEVKIT_V1.Pin_19, ESP_32-C6_DEVKIT_V1.Pin_30, DRIVER_HBS860H.1
  Q2: ESP_32-C6_DEVKIT_V1.Pin_20, DRIVER_HBS860H.2
  Q3: ESP_32-C6_DEVKIT_V1.Pin_21, DRIVER_HBS860H.4
  NC DOWN: ESP_32-C6_DEVKIT_V1.Pin_28
  NC UP: ESP_32-C6_DEVKIT_V1.Pin_29
  N2: STEP_DOWN_5V.IN+, PSU_48V.4
  N3: STEP_DOWN_5V.IN-, PSU_48V.2
  5V: STEP_DOWN_5V.OUT+, LCD_20X4.VCC, DRIVER_HBS860H.3, DRIVER_HBS860H.5, DRIVER_HBS860H.6
  GND: STEP_DOWN_5V.OUT-, SENSOR_SUDUT_AS5600.Pin_3, LCD_20X4.GND, BACK.leg1, STOP.leg1, MODE.leg1, OK.leg1, ZERO.leg1, LIMIT_ATAS.NC, LIMIT_BAWAH.NC, Q1.E, Q2.E, Q3.E, R4.Pin_0, R5.Pin_0, R6.Pin_0
  GND DRIVER: PSU_48V.1
  N4: PSU_48V.3, E-STOP.leg0
  VCC DRIVER: E-STOP.leg1
  3V3: SENSOR_SUDUT_AS5600.Pin_1
  GPI04: SENSOR_SUDUT_AS5600.Pin_5
  GPIO5: SENSOR_SUDUT_AS5600.Pin_6, LCD_20X4.SCL
  GPIO4: LCD_20X4.SDA
  GPIO1: BACK.leg0
  GPIO10: STOP.leg0
  GPIO11: MODE.leg0
  GPIO12: OK.leg0
  GPIO13: ZERO.leg0
  GPIO2: LIMIT_ATAS.C
  GPIO3: LIMIT_BAWAH.C
  N5: Q1.B, R1.Pin_1, R4.Pin_1
  PUL-: Q1.C
  N6: Q2.B, R2.Pin_1, R5.Pin_1
  DIR-: Q2.C
  N7: Q3.B, R3.Pin_1, R6.Pin_1
  ENA-: Q3.C
  GPIO18: R1.Pin_0
  GPIO19: R2.Pin_0
  GPIO20: R3.Pin_0

notes:
  POWER SUPPLY SYSTEM
  MIKROKONTROLER ESP32-C6
  RANGKAIAN INTERFACE OPEN COLLECTOR DRIVER
  RANGKAIAN LCD DAN PUSH BUTTON
  RANGKAIAN AS5600 DAN LIMIT SWITCH
  SISTEM REHABILITASI LENGAN 1 DOF

custom parts:
  ESP32-C6 devkit: ESP32 / ESP32-C6 WiFi+Bluetooth Internet Of Things Dual Type-C Development Board Core Board ESP32-C6-DevKit.
  AS5600 module: .This module is mainly placed behind the stepper motor to obtain the rotation angle of the stepper motor.
  LCD2004-I2C: A standard character display with 4x20 characters. Comes in many colors with LCM2004 IIC attached.
  JL012-13-5.2 Lever (Limit) Switch SPDT + NO + NC: Micro Switch; Model No.: JL012-13.5-2; Actuator Action: Momentary; Actuator Type: Hinge Lever; Contact Configuration: 1NO, 1NC (SPDT) Temperature -25~65℃；Relative humidity: below 85%; Rate Voltage: 125V AC; Rated Current: 1A.
